// Logisim project stack_logical_normal.circ as structural Verilog: 12 circuits, main circuit main
module main (
  input  [1:0] COMMAND,
  input  CLK,
  input  RESET,
  input  [2:0] INDEX,
  input  [3:0] IO_DATA_in,
  output [3:0] IO_DATA_out
);

  stack stack_1 (
    .COMMAND(COMMAND), .CLK(CLK), .RESET(RESET), .INDEX(INDEX), .IO_DATA_in(IO_DATA_in),
    .IO_DATA_out(IO_DATA_out));
endmodule

module twoToFour (
  input  A0,
  input  A1,
  output Q0,
  output Q1,
  output Q2,
  output Q3
);

  wire not_1_out, not_2_out, not_3_out, not_4_out;

  not not_1 (not_1_out, A0);
  not not_2 (not_2_out, A1);
  not not_3 (not_3_out, A1);
  not not_4 (not_4_out, A0);
  and and_1 (Q0, not_1_out, not_2_out);
  and and_2 (Q1, A0, not_3_out);
  and and_3 (Q2, not_4_out, A1);
  and and_4 (Q3, A0, A1);
endmodule

module RStrigger (
  input  R,
  input  C,
  input  S,
  input  reset,
  output Q,
  output notQ
);

  wire and_1_out, and_2_out, nor_2_out;

  and and_1 (and_1_out, R, C);
  and and_2 (and_2_out, C, S);
  nor nor_1 (Q, and_1_out, notQ);
  nor nor_2 (nor_2_out, Q, and_2_out);
  or or_1 (notQ, nor_2_out, reset);
endmodule

module Dtrigger (
  input  D,
  input  C,
  input  reset,
  output Q,
  output notQ
);

  wire not_1_out;

  not not_1 (not_1_out, D);
  RStrigger rstrigger_1 (.R(not_1_out), .C(C), .S(D), .reset(reset), .Q(Q), .notQ(notQ));
endmodule

module counterMod5next (
  input  plusOrMinus,
  input  C,
  input  reset,
  output [4:0] Q
);

  wire and_1_out, and_2_out, and_3_out, and_4_out, and_5_out, and_6_out, and_7_out, and_8_out, and_9_out,
       and_10_out, not_1_out, or_1_out, or_2_out, or_3_out, or_4_out, or_5_out, or_6_out, or_7_out;

  not not_1 (not_1_out, plusOrMinus);
  and and_1 (and_1_out, Q[4], not_1_out);
  and and_2 (and_2_out, plusOrMinus, Q[1]);
  or or_1 (or_1_out, and_1_out, and_2_out);
  and and_3 (and_3_out, Q[0], not_1_out);
  and and_4 (and_4_out, plusOrMinus, Q[2]);
  and and_5 (and_5_out, Q[1], not_1_out);
  and and_6 (and_6_out, plusOrMinus, Q[3]);
  and and_7 (and_7_out, Q[2], not_1_out);
  and and_8 (and_8_out, plusOrMinus, Q[4]);
  and and_9 (and_9_out, Q[3], not_1_out);
  and and_10 (and_10_out, plusOrMinus, Q[0]);
  or or_2 (or_2_out, or_1_out, reset);
  or or_3 (or_3_out, and_3_out, and_4_out);
  or or_4 (or_4_out, and_5_out, and_6_out);
  or or_5 (or_5_out, and_7_out, and_8_out);
  or or_6 (or_6_out, and_9_out, and_10_out);
  or or_7 (or_7_out, C, reset);
  DtriggerFront dtriggerfront_1 (.D(or_2_out), .C(or_7_out), .reset(reset), .Q(Q[0]));  // open: notQ
  DtriggerFront dtriggerfront_2 (.D(or_3_out), .C(C), .reset(reset), .Q(Q[1]));  // open: notQ
  DtriggerFront dtriggerfront_3 (.D(or_4_out), .C(C), .reset(reset), .Q(Q[2]));  // open: notQ
  DtriggerFront dtriggerfront_4 (.D(or_5_out), .C(C), .reset(reset), .Q(Q[3]));  // open: notQ
  DtriggerFront dtriggerfront_5 (.D(or_6_out), .C(C), .reset(reset), .Q(Q[4]));  // open: notQ
endmodule

module DtriggerFront (
  input  D,
  input  C,
  input  reset,
  output Q,
  output notQ
);

  wire dtrigger_1_q, not_1_out;

  Dtrigger dtrigger_1 (.D(D), .C(C), .reset(reset), .Q(dtrigger_1_q));  // open: notQ
  not not_1 (not_1_out, C);
  Dtrigger dtrigger_2 (.D(dtrigger_1_q), .C(not_1_out), .reset(reset), .Q(Q), .notQ(notQ));
endmodule

module mem (
  input  D0,
  input  D1,
  input  D2,
  input  D3,
  input  ReadOrWrite,
  input  C,
  input  reset,
  output Q0,
  output Q1,
  output Q2,
  output Q3
);

  wire and_1_out;

  and and_1 (and_1_out, ReadOrWrite, C);
  Dtrigger dtrigger_1 (.D(D0), .C(and_1_out), .reset(reset), .Q(Q0));  // open: notQ
  Dtrigger dtrigger_2 (.D(D1), .C(and_1_out), .reset(reset), .Q(Q1));  // open: notQ
  Dtrigger dtrigger_3 (.D(D2), .C(and_1_out), .reset(reset), .Q(Q2));  // open: notQ
  Dtrigger dtrigger_4 (.D(D3), .C(and_1_out), .reset(reset), .Q(Q3));  // open: notQ
endmodule

module stack (
  input  [1:0] COMMAND,
  input  CLK,
  input  RESET,
  input  [2:0] INDEX,
  input  [3:0] IO_DATA_in,
  output [3:0] IO_DATA_out
);

  wire and_1_out, and_2_out, and_3_out, and_4_out, and_5_out, and_6_out, and_7_out, and_8_out, and_9_out,
       and_10_out, and_11_out, and_12_out, and_13_out, and_14_out, and_15_out, and_16_out, and_17_out,
       and_18_out, and_19_out, and_20_out, and_21_out, and_22_out, and_23_out, and_24_out, and_25_out,
       and_26_out, and_27_out, mem_1_q0, mem_1_q1, mem_1_q2, mem_1_q3, mem_2_q0, mem_2_q1, mem_2_q2,
       mem_2_q3, mem_3_q0, mem_3_q1, mem_3_q2, mem_3_q3, mem_4_q0, mem_4_q1, mem_4_q2, mem_4_q3, mem_5_q0,
       mem_5_q1, mem_5_q2, mem_5_q3, not_1_out, not_2_out, not_3_out, or_1_out, twotofour_1_q0,
       twotofour_1_q1, twotofour_1_q2, twotofour_1_q3;
  wire [3:0] or_2_out;
  wire [4:0] countermod5current_1_q, countermod5next_1_q, oneoftwo_1_result, oneoftwo_2_result,
       substractormod5_1_q;

  twoToFour twotofour_1 (
    .A0(COMMAND[0]), .A1(COMMAND[1]), .Q0(twotofour_1_q0), .Q1(twotofour_1_q1), .Q2(twotofour_1_q2),
    .Q3(twotofour_1_q3));
  not not_1 (not_1_out, twotofour_1_q0);
  not not_2 (not_2_out, twotofour_1_q3);
  and and_1 (and_1_out, not_1_out, not_2_out, CLK);
  counterMod5next countermod5next_1 (
    .plusOrMinus(twotofour_1_q2), .C(and_1_out), .reset(RESET), .Q(countermod5next_1_q));
  counterMod5current countermod5current_1 (
    .plusOrMinus(twotofour_1_q2), .C(and_1_out), .reset(RESET), .Q(countermod5current_1_q));
  SubstractorMod5 substractormod5_1 (.counter(countermod5next_1_q), .INDEX(INDEX), .Q(substractormod5_1_q));
  and and_2 (and_2_out, twotofour_1_q1, countermod5next_1_q[0]);
  and and_3 (and_3_out, twotofour_1_q1, countermod5next_1_q[1]);
  and and_4 (and_4_out, twotofour_1_q1, countermod5next_1_q[2]);
  and and_5 (and_5_out, twotofour_1_q1, countermod5next_1_q[3]);
  and and_6 (and_6_out, twotofour_1_q1, countermod5next_1_q[4]);
  oneOfTwo oneoftwo_1 (
    .A(countermod5next_1_q), .AorB(twotofour_1_q2), .B(countermod5current_1_q), .result(oneoftwo_1_result));
  oneOfTwo oneoftwo_2 (
    .A(oneoftwo_1_result), .AorB(twotofour_1_q3), .B(substractormod5_1_q), .result(oneoftwo_2_result));
  or or_1 (or_1_out, twotofour_1_q3, twotofour_1_q2);
  and and_7 (and_7_out, or_1_out, CLK);
  mem mem_1 (
    .D0(IO_DATA_in[0]), .D1(IO_DATA_in[1]), .D2(IO_DATA_in[2]), .D3(IO_DATA_in[3]), .ReadOrWrite(and_2_out),
    .C(and_1_out), .reset(RESET), .Q0(mem_1_q0), .Q1(mem_1_q1), .Q2(mem_1_q2), .Q3(mem_1_q3));
  mem mem_2 (
    .D0(IO_DATA_in[0]), .D1(IO_DATA_in[1]), .D2(IO_DATA_in[2]), .D3(IO_DATA_in[3]), .ReadOrWrite(and_3_out),
    .C(and_1_out), .reset(RESET), .Q0(mem_2_q0), .Q1(mem_2_q1), .Q2(mem_2_q2), .Q3(mem_2_q3));
  mem mem_3 (
    .D0(IO_DATA_in[0]), .D1(IO_DATA_in[1]), .D2(IO_DATA_in[2]), .D3(IO_DATA_in[3]), .ReadOrWrite(and_4_out),
    .C(and_1_out), .reset(RESET), .Q0(mem_3_q0), .Q1(mem_3_q1), .Q2(mem_3_q2), .Q3(mem_3_q3));
  mem mem_4 (
    .D0(IO_DATA_in[0]), .D1(IO_DATA_in[1]), .D2(IO_DATA_in[2]), .D3(IO_DATA_in[3]), .ReadOrWrite(and_5_out),
    .C(and_1_out), .reset(RESET), .Q0(mem_4_q0), .Q1(mem_4_q1), .Q2(mem_4_q2), .Q3(mem_4_q3));
  mem mem_5 (
    .D0(IO_DATA_in[0]), .D1(IO_DATA_in[1]), .D2(IO_DATA_in[2]), .D3(IO_DATA_in[3]), .ReadOrWrite(and_6_out),
    .C(and_1_out), .reset(RESET), .Q0(mem_5_q0), .Q1(mem_5_q1), .Q2(mem_5_q2), .Q3(mem_5_q3));
  and and_8 (and_8_out, mem_1_q0, oneoftwo_2_result[0]);
  and and_9 (and_9_out, mem_2_q0, oneoftwo_2_result[1]);
  and and_10 (and_10_out, mem_3_q0, oneoftwo_2_result[2]);
  and and_11 (and_11_out, mem_4_q0, oneoftwo_2_result[3]);
  and and_12 (and_12_out, mem_5_q0, oneoftwo_2_result[4]);
  and and_13 (and_13_out, mem_1_q1, oneoftwo_2_result[0]);
  and and_14 (and_14_out, mem_2_q1, oneoftwo_2_result[1]);
  and and_15 (and_15_out, mem_3_q1, oneoftwo_2_result[2]);
  and and_16 (and_16_out, mem_4_q1, oneoftwo_2_result[3]);
  and and_17 (and_17_out, mem_5_q1, oneoftwo_2_result[4]);
  and and_18 (and_18_out, mem_1_q2, oneoftwo_2_result[0]);
  and and_19 (and_19_out, mem_2_q2, oneoftwo_2_result[1]);
  and and_20 (and_20_out, mem_3_q2, oneoftwo_2_result[2]);
  and and_21 (and_21_out, mem_4_q2, oneoftwo_2_result[3]);
  and and_22 (and_22_out, mem_5_q2, oneoftwo_2_result[4]);
  and and_23 (and_23_out, mem_1_q3, oneoftwo_2_result[0]);
  and and_24 (and_24_out, mem_2_q3, oneoftwo_2_result[1]);
  and and_25 (and_25_out, mem_3_q3, oneoftwo_2_result[2]);
  and and_26 (and_26_out, mem_4_q3, oneoftwo_2_result[3]);
  and and_27 (and_27_out, mem_5_q3, oneoftwo_2_result[4]);
  or or_2 (or_2_out[0], and_8_out, and_9_out, and_10_out, and_11_out, and_12_out);
  or or_3 (or_2_out[1], and_13_out, and_14_out, and_15_out, and_16_out, and_17_out);
  or or_4 (or_2_out[2], and_18_out, and_19_out, and_20_out, and_21_out, and_22_out);
  or or_5 (or_2_out[3], and_23_out, and_24_out, and_25_out, and_26_out, and_27_out);
  // Probe on IO_DATA_in
  not not_3 (not_3_out, and_7_out);
  Transistor #(.\type ("n"), .width(4)) transistor_1 (.in(or_2_out), .out(IO_DATA_in), .gate(and_7_out));
  Transistor #(.width(4)) transistor_2 (.in(or_2_out), .out(IO_DATA_in), .gate(not_3_out));

  assign IO_DATA_out = IO_DATA_in;
endmodule

module SubstractorMod5 (
  input  [4:0] counter,
  input  [2:0] INDEX,
  output [4:0] Q
);

  wire and_1_out, and_2_out, and_3_out, and_4_out, and_5_out, and_6_out, and_7_out, and_8_out, and_9_out,
       and_10_out, and_11_out, and_12_out, and_13_out, and_14_out, and_15_out, and_16_out, and_17_out,
       and_18_out, and_19_out, and_20_out, and_21_out, and_22_out, and_23_out, and_24_out, and_25_out,
       mod5_1_q0, mod5_1_q1, mod5_1_q2, mod5_1_q3, mod5_1_q4;

  mod5 mod5_1 (.INDEX(INDEX), .Q0(mod5_1_q0), .Q1(mod5_1_q1), .Q2(mod5_1_q2), .Q3(mod5_1_q3), .Q4(mod5_1_q4));
  and and_1 (and_1_out, counter[1], mod5_1_q0);
  and and_2 (and_2_out, counter[2], mod5_1_q0);
  and and_3 (and_3_out, counter[3], mod5_1_q0);
  and and_4 (and_4_out, counter[4], mod5_1_q0);
  and and_5 (and_5_out, counter[0], mod5_1_q0);
  and and_6 (and_6_out, counter[2], mod5_1_q1);
  and and_7 (and_7_out, counter[3], mod5_1_q1);
  and and_8 (and_8_out, counter[4], mod5_1_q1);
  and and_9 (and_9_out, counter[0], mod5_1_q1);
  and and_10 (and_10_out, counter[1], mod5_1_q1);
  and and_11 (and_11_out, counter[3], mod5_1_q2);
  and and_12 (and_12_out, counter[4], mod5_1_q2);
  and and_13 (and_13_out, counter[0], mod5_1_q2);
  and and_14 (and_14_out, counter[1], mod5_1_q2);
  and and_15 (and_15_out, counter[2], mod5_1_q2);
  and and_16 (and_16_out, counter[4], mod5_1_q3);
  and and_17 (and_17_out, counter[0], mod5_1_q3);
  and and_18 (and_18_out, counter[1], mod5_1_q3);
  and and_19 (and_19_out, counter[2], mod5_1_q3);
  and and_20 (and_20_out, counter[3], mod5_1_q3);
  and and_21 (and_21_out, counter[0], mod5_1_q4);
  and and_22 (and_22_out, counter[1], mod5_1_q4);
  and and_23 (and_23_out, counter[2], mod5_1_q4);
  and and_24 (and_24_out, counter[3], mod5_1_q4);
  and and_25 (and_25_out, counter[4], mod5_1_q4);
  or or_1 (Q[0], and_1_out, and_6_out, and_11_out, and_16_out, and_21_out);
  or or_2 (Q[1], and_2_out, and_7_out, and_12_out, and_17_out, and_22_out);
  or or_3 (Q[2], and_3_out, and_8_out, and_13_out, and_18_out, and_23_out);
  or or_4 (Q[3], and_4_out, and_9_out, and_14_out, and_19_out, and_24_out);
  or or_5 (Q[4], and_5_out, and_10_out, and_15_out, and_20_out, and_25_out);
endmodule

module mod5 (
  input  [2:0] INDEX,
  output Q0,
  output Q1,
  output Q2,
  output Q3,
  output Q4
);

  wire and_1_out, and_2_out, and_3_out, not_1_out, not_2_out, not_3_out, not_4_out, not_5_out, not_6_out,
       not_7_out, not_8_out, not_9_out, not_10_out, not_11_out, not_12_out, not_13_out, not_14_out,
       not_15_out, or_1_out, or_2_out, xor_1_out;

  not not_1 (not_1_out, INDEX[0]);
  not not_2 (not_2_out, INDEX[1]);
  or or_1 (or_1_out, INDEX[0], INDEX[1]);
  not not_3 (not_3_out, INDEX[1]);
  and and_1 (and_1_out, INDEX[2], not_4_out);
  not not_4 (not_4_out, INDEX[0]);
  and and_2 (and_2_out, not_1_out, not_2_out, INDEX[2]);
  and and_3 (and_3_out, INDEX[2], or_1_out);
  or or_2 (or_2_out, not_3_out, and_1_out);
  xor xor_1 (xor_1_out, INDEX[0], and_3_out);
  not not_5 (not_5_out, or_2_out);
  not not_6 (not_6_out, xor_1_out);
  not not_7 (not_7_out, not_5_out);
  not not_8 (not_8_out, and_2_out);
  not not_9 (not_9_out, not_5_out);
  not not_10 (not_10_out, and_2_out);
  not not_11 (not_11_out, xor_1_out);
  not not_12 (not_12_out, and_2_out);
  not not_13 (not_13_out, and_2_out);
  not not_14 (not_14_out, xor_1_out);
  not not_15 (not_15_out, not_5_out);
  and and_4 (Q0, not_6_out, not_7_out, not_8_out);
  and and_5 (Q1, xor_1_out, not_9_out, not_10_out);
  and and_6 (Q2, not_11_out, not_5_out, not_12_out);
  and and_7 (Q3, xor_1_out, not_5_out, not_13_out);
  and and_8 (Q4, not_14_out, not_15_out, and_2_out);
endmodule

module counterMod5current (
  input  plusOrMinus,
  input  C,
  input  reset,
  output [4:0] Q
);

  wire and_1_out, and_2_out, and_3_out, and_4_out, and_5_out, and_6_out, and_7_out, and_8_out, and_9_out,
       and_10_out, not_1_out, or_1_out, or_2_out, or_3_out, or_4_out, or_5_out, or_6_out, or_7_out;

  not not_1 (not_1_out, plusOrMinus);
  and and_1 (and_1_out, Q[4], not_1_out);
  and and_2 (and_2_out, plusOrMinus, Q[1]);
  and and_3 (and_3_out, Q[3], not_1_out);
  and and_4 (and_4_out, plusOrMinus, Q[0]);
  or or_1 (or_1_out, and_1_out, and_2_out);
  and and_5 (and_5_out, Q[0], not_1_out);
  and and_6 (and_6_out, plusOrMinus, Q[2]);
  and and_7 (and_7_out, Q[1], not_1_out);
  and and_8 (and_8_out, plusOrMinus, Q[3]);
  and and_9 (and_9_out, Q[2], not_1_out);
  and and_10 (and_10_out, plusOrMinus, Q[4]);
  or or_2 (or_2_out, and_3_out, and_4_out);
  or or_3 (or_3_out, and_5_out, and_6_out);
  or or_4 (or_4_out, and_7_out, and_8_out);
  or or_5 (or_5_out, and_9_out, and_10_out);
  or or_6 (or_6_out, or_2_out, reset);
  or or_7 (or_7_out, C, reset);
  DtriggerFront dtriggerfront_1 (.D(or_1_out), .C(C), .reset(reset), .Q(Q[0]));  // open: notQ
  DtriggerFront dtriggerfront_2 (.D(or_3_out), .C(C), .reset(reset), .Q(Q[1]));  // open: notQ
  DtriggerFront dtriggerfront_3 (.D(or_4_out), .C(C), .reset(reset), .Q(Q[2]));  // open: notQ
  DtriggerFront dtriggerfront_4 (.D(or_5_out), .C(C), .reset(reset), .Q(Q[3]));  // open: notQ
  DtriggerFront dtriggerfront_5 (.D(or_6_out), .C(or_7_out), .reset(reset), .Q(Q[4]));  // open: notQ
endmodule

module oneOfTwo (
  input  [4:0] A,
  input  AorB,
  input  [4:0] B,
  output [4:0] result
);

  wire and_1_out, and_2_out, and_3_out, and_4_out, and_5_out, and_6_out, and_7_out, and_8_out, and_9_out,
       and_10_out, not_1_out;

  not not_1 (not_1_out, AorB);
  and and_1 (and_1_out, A[0], not_1_out);
  and and_2 (and_2_out, AorB, B[0]);
  and and_3 (and_3_out, A[1], not_1_out);
  and and_4 (and_4_out, AorB, B[1]);
  and and_5 (and_5_out, A[2], not_1_out);
  and and_6 (and_6_out, AorB, B[2]);
  and and_7 (and_7_out, A[3], not_1_out);
  and and_8 (and_8_out, AorB, B[3]);
  and and_9 (and_9_out, A[4], not_1_out);
  and and_10 (and_10_out, AorB, B[4]);
  or or_1 (result[0], and_1_out, and_2_out);
  or or_2 (result[1], and_3_out, and_4_out);
  or or_3 (result[2], and_5_out, and_6_out);
  or or_4 (result[3], and_7_out, and_8_out);
  or or_5 (result[4], and_9_out, and_10_out);
endmodule
